// Logisim project 7.circ as structural Verilog: 1 circuit, main circuit main
module main (
  input  in_1,
  input  in_2,
  output out_3,
  output out_4
);

  buf xor_1 (out_3, in_2);  // XOR_Gate
  and and_1 (out_4, in_2, in_1);
endmodule
